# Fritzing sketch Breadboard (saved by Fritzing 0.9.3b)
breadboards: 1

parts:
  U1 = LCD-16X2 [package=lcd-16x2]
  R2 = Rotary Potentiometer (Small) [maximum_resistance=100kΩ package=THT]
  Raspberry_Pi_1 = Raspberry Pi 3 [part_number=RPI-3-V1.2]
  R3 = Resistor [tolerance=±5% resistance=220 package="2010 [SMD]"]
  RHT1 = Humidity and Temperature Sensor RHT03  # not connected

nets:
  N1: U1.A, R3.Pin_0
  N2: U1.K, R2.leg2, Raspberry_Pi_1.GND
  N3: R2.leg1, Raspberry_Pi_1.5V, R3.Pin_1
